# Fritzing sketch openMIDIStomper (saved by Fritzing 0.9.9b)
breadboards: 1

parts:
  S2 = Round Pushbutton
  LED1 = LED - 5mm [color="Red (633nm)" current=0.030 package="5 mm [THT]"]
  S3 = Round Pushbutton
  LED2 = LED - 5mm [color="Red (633nm)" current=0.030 package="5 mm [THT]"]
  S4 = Round Pushbutton
  S5 = Round Pushbutton
  LED3 = LED - 5mm [color="Red (633nm)" current=0.030 package="5 mm [THT]"]
  LED4 = LED - 5mm [color="Red (633nm)" current=0.030 package="5 mm [THT]"]
  LED5 = LED - 5mm [color="Red (633nm)" current=0.030 package="5 mm [THT]"]
  LED6 = LED - 5mm [color="Red (633nm)" current=0.030 package="5 mm [THT]"]
  LED7 = LED - 5mm [color="Red (633nm)" current=0.030 package="5 mm [THT]"]
  LED8 = LED - 5mm [color="Red (633nm)" current=0.030 package="5 mm [THT]"]
  R1 = Resistor [tolerance=±5% power=0.25 resistance=220 package=THT]  # not connected
  R2 = Resistor [tolerance=±5% power=0.25 resistance=220 package=THT]  # not connected
  R3 = Resistor [tolerance=±5% power=0.25 resistance=220 package=THT]  # not connected
  R4 = Resistor [tolerance=±5% power=0.25 resistance=220 package=THT]  # not connected
  R5 = Resistor [tolerance=±5% power=0.25 resistance=220 package=THT]  # not connected
  R6 = Resistor [tolerance=±5% power=0.25 resistance=220 package=THT]  # not connected
  R7 = Resistor [tolerance=±5% power=0.25 resistance=220 package=THT]  # not connected
  R9 = Resistor [tolerance=±5% power=0.25 resistance=220 package=THT]  # not connected
  S6 = Round Pushbutton
  S7 = Round Pushbutton
  S8 = Round Pushbutton
  S9 = Round Pushbutton
  Pro_Micro4 = Pro Micro  # not connected
  TRS2 = Audio Jack (TRS) 3.5mm [package="4Ucon 08780 [THT]"]
  TRS3 = Audio Jack (TRS) 3.5mm [package="4Ucon 08780 [THT]"]

nets:
  N1: S2.leg0, S6.leg0
  N2: S2.leg1, S3.leg1, S4.leg1, S5.leg1
  N3: LED1.cathode, LED2.cathode, LED3.cathode, LED4.cathode, LED5.cathode, LED6.cathode, LED7.cathode, LED8.cathode, TRS2.Sleeve, TRS3.Sleeve
  N4: S3.leg0, S7.leg0
  N5: S4.leg0, S9.leg0
  N6: S5.leg0, S8.leg0
  N7: S6.leg1, S7.leg1, S8.leg1, S9.leg1
  N8: TRS2.Ring, TRS3.Ring

notes:
  220Ω
  MIDI Pedal Board
  by Gustavo Silveira
  A.k.a. Nerd Musician
  go.musiconerd.com
  T - Wiper
  R - 5V
  S - GND

custom parts:
  Pro Micro: The SparkFun Pro Micro is a complete USB-based microcontoller development system, in a very small footprint, capable of implementing many types of projects. All programming can be done via the USB port.
